// Logisim project mips-processor-with pipeline.circ as structural Verilog: 25 circuits, main circuit main
// MEM/WB
module main (
  input  in_1,
  output [31:0] out_2,
  output [1:0] out_3,
  output [25:0] out_4,
  output [31:0] out_5,
  output [31:0] out_6,
  output [3:0] out_7,
  output [31:0] out_8,
  output [1:0] out_9,
  output [3:0] out_10,
  output [25:0] out_11,
  output [25:0] out_12,
  output [25:0] out_13
);

  wire adder_1_cout, B_flush, BEZ_2, BGEZ_2, BGTZ_2, BLEZ_2, BLTZ_2, BNE_2, BNEZ_2, BRANCH_2, clock_1_out,
       J_flush, J_stall, Load_stall, not_1_out, or_1_out, or_2_out, or_3_out, pc_src, zergtz, zero, zeroeqz,
       zerogez, zerolez, zeroltz;
  wire [1:0] ALUSRC_2, funct1;
  wire [2:0] Ra, Rb, RD1, RD2, RD3, RD_t, RS1, RS2, RT1, RT2;
  wire [3:0] ALUOP_2;
  wire [4:0] imm5__1, INPUT_CONTROL;
  wire [7:0] _8imm, _8imm__1;
  wire [10:0] _11imm__1;
  wire [10:8] _11imm;
  wire [15:0] ram_1_data;
  wire [19:0] btanch_1_out_branch, jump_1_jumpoutput, multiplexer_6_out, next_pc, pc, pc1, pc2, pc___2,
       pc__id;
  wire [25:0] control_2, multiplexer_5_out;
  wire [31:0] ALU_OUT, bit_extender_1_out, bit_extender_2_out, bit_extender_3_out, bus_a, bus_a_1, bus_a_2,
       bus_b, bus_b_1, bus_b_2, mem_wb_1_mem_out_2, multiplexer_4_out, multiplexer_8_out, multiplexer_9_out,
       multiplexer_10_out, ram_2_data, result;

  not not_1 (not_1_out, Load_stall);
  Register #(.width(20)) u_PC (.D(next_pc), .en(not_1_out), .Q(pc), .clk(clock_1_out), .clr(in_1));
  Clock clock_1 (.out(clock_1_out));
  control_unit control_unit_1 (
    .REG_DST(out_11[0]), .REGWRITE(out_11[1]), .ALUOP(out_11[5:2]), .ALUSRC(out_11[7:6]), .JUMP(out_11[8]),
    .JSELECT(out_11[9]), .LINK(out_11[10]), .BRANCH(out_11[11]), .BNE(out_11[12]), .BEZ(out_11[13]),
    .BLTZ(out_11[16]), .BGEZ(out_11[17]), .BGTZ(out_11[18]), .BLEZ(out_11[19]), .BNEZ(out_11[20]),
    .MOMREAD(out_11[21]), .MOMWRITE(out_11[22]), .MOMREG(out_11[23]), .SELECT(out_11[24]),
    .SHIFT(out_11[15:14]), .in_1(INPUT_CONTROL), .dst2(out_11[25]));
  RAM #(.addrWidth(20), .dataWidth(16)) ram_1 (
    .addr(pc), .data(ram_1_data), .clk(clock_1_out), .clr(in_1));  // open: sel, ld
  IF_ID if_id_1 (
    .Next_pc1(pc), .ins(ram_1_data), .clr(B_flush), .Next_pc_1(pc__id),
    .ins_2({INPUT_CONTROL, _11imm, _8imm}), .clock(clock_1_out));
  Hazerd_Unit hazerd_unit_1 (
    .ID_EX_Jump(out_11[8]), .ID_EX_MemRead(out_13[21]), .IF_ID_Rt(_8imm[4:2]), .LoadStall(Load_stall),
    .ID_EX_Rd(RD1), .IF_ID_Rs(_8imm[7:5]), .b(pc_src), .JumpFlush(J_flush), .JumpStall(J_stall),
    .b_flush(B_flush));
  Multiplexer #(.width(3), .enable("false")) multiplexer_1 (.in0(_11imm), .in1(3'b111), .out(RD_t), .sel(out_11[10]));
  Multiplexer #(.width(3), .enable("false")) multiplexer_2 (.in0(_8imm[7:5]), .in1(RD_t), .out(Rb), .sel(out_11[25]));
  Multiplexer #(.width(3), .enable("false")) multiplexer_3 (.in0(_8imm[4:2]), .in1(RD_t), .out(Ra), .sel(out_11[0]));
  or or_1 (or_1_out, J_stall, Load_stall);
  Adder #(.width(20)) adder_1 (.a(pc), .b(20'h2), .out(pc___2), .cout(adder_1_cout));  // open: cin
  Register_File register_file_1 (
    .Rt(Ra), .Rs(Rb), .RD(RD3), .RegWrite(out_4[1]), .BUS_W(multiplexer_4_out), .BUS_A(bus_a), .BUS_B(bus_b),
    .in_6(clock_1_out));
  Multiplexer #(.width(32), .enable("false")) multiplexer_4 (
    .in0(result), .in1(bit_extender_1_out), .out(multiplexer_4_out), .sel(out_11[10]));
  assign bit_extender_1_out = {{12{pc___2[19]}}, pc___2};  // Bit_Extender bit_extender_1
  btanch btanch_1 (
    .BRANCH(out_13[11]), .zer0(zero), .BNE(out_13[12]), .BEQZ(out_13[13]), .zero_eqz(zeroeqz),
    .BNEZ(out_13[20]), .BLTZ(out_13[16]), .zero_ltz(zeroltz), .BGEZ(out_13[17]), .zero_gez(zerogez),
    .BGTZ(out_13[18]), .zero_gtz(zergtz), .BLEZ(out_13[19]), .zero_lez(zerolez), .pcsrc(pc_src),
    ._5IMM(_8imm[4:0]), ._8IMM(_8imm), .PC(pc), .SELECT(out_13[24]), .out_branch(btanch_1_out_branch));
  JUMP jump_1 (
    ._11_imm(_11imm__1), .pc(pc), .reg_rd(bus_b_1), ._8imm(_8imm__1), .jumpoutput(jump_1_jumpoutput),
    .JSELSCT(out_13[9]));
  Multiplexer #(.width(26), .enable("false")) multiplexer_5 (
    .in0(out_11), .in1({26{1'b0}}), .out(multiplexer_5_out), .sel(or_1_out));
  Multiplexer #(.width(20), .enable("false")) multiplexer_6 (
    .in0(pc___2), .in1(btanch_1_out_branch), .out(multiplexer_6_out), .sel(pc_src));
  Forward__Unit forward_unit_1 (
    .Forward_A(out_3), .Forward_B(out_9), .RegWrt_WB(out_11[1]), .RegWrt_Mem_WB(out_4[1]),
    .RegWrt_Ex_Mem(control_2[1]), .Ra(Ra), .Rb(Rb), .Mem_WB_Rd(RD3), .Ex_Mem_Rd(RD2), .Rd_WB(RD1));
  ID_EX id_ex_1 (
    .Next_pc_2(pc__id), .i_imm(_8imm[4:0]), .bus_a(bus_a), .bus_b(bus_b), .Rs(Rb), .Rt(Ra), .Rd(RD_t),
    .J_imm_11({_11imm, _8imm}), .B_imm(_8imm), .control_1(multiplexer_5_out), .Next_pc2(pc1),
    .i_imm1(imm5__1), .bus_a_2(bus_a_1), .bus_b_2(bus_b_1), .Rs_Ex(RS1), .Rt_Ex(RT1), .Rd_Ex(RD1),
    .J_imm1(_11imm__1), .B_imm1(_8imm__1), .control_2(out_13), .CLK(clock_1_out), .clr(or_2_out),
    .fu(_8imm[1:0]), .fu2(funct1));
  or or_2 (or_2_out, B_flush, J_flush);
  Multiplexer #(.width(20), .enable("false")) multiplexer_7 (
    .in0(multiplexer_6_out), .in1(jump_1_jumpoutput), .out(next_pc), .sel(out_11[8]));
  assign bit_extender_2_out = {{27{1'b0}}, imm5__1};  // Bit_Extender bit_extender_2
  assign bit_extender_3_out = {{24{1'b0}}, _8imm__1};  // Bit_Extender bit_extender_3
  Multiplexer #(.select(2), .width(32), .enable("false")) multiplexer_8 (
    .in0(bit_extender_2_out), .in1(bit_extender_3_out), .in2(bus_b_1), .in3({32{1'b0}}),
    .out(multiplexer_8_out), .sel(out_13[7:6]));
  ALUCONTROL alucontrol_1 (.aluop(out_13[5:2]), .funct(funct1), .out_3(out_7));
  Multiplexer #(.select(2), .width(32), .enable("false")) multiplexer_9 (
    .in0(multiplexer_8_out), .in1(ALU_OUT), .in2(result), .in3(result), .out(multiplexer_9_out), .sel(out_3));
  Multiplexer #(.select(2), .width(32), .enable("false")) multiplexer_10 (
    .in0(bus_a_1), .in1(ALU_OUT), .in2(result), .in3(result), .out(multiplexer_10_out), .sel(out_9));
  ALU alu_1 (
    .RT(multiplexer_9_out), .RS(multiplexer_10_out), .shift(out_13[15:14]), .alu_in(out_7),
    .output_alu(out_2), .zero(zero), .zerogtz(zergtz), .zeroeqz(zeroeqz), .zeroltz(zeroltz),
    .zerogez(zerogez), .zerolez(zerolez));
  EX_MEM ex_mem_1 (
    .Control(out_13), .PC(pc1), .BUS_A(bus_a_1), .ALU_OUT(out_2), .BUS_B(bus_b_1), .RS(RS1), .Rd(RD1),
    .RT(RT1), .PC_2(pc2), .BUS_A2(bus_a_2), .ALU_out_2(out_6), .BUS_B2(bus_b_2), .RS_minus(RS2),
    .Rd_minus(RD2), .RT_minus(RT2), .clk(clock_1_out), .clr(or_3_out),
    .control_2({control_2[25:21], BNEZ_2, BLEZ_2, BGTZ_2, BGEZ_2, BLTZ_2, control_2[15:14], BEZ_2, BNE_2, BRANCH_2, control_2[10:8], ALUSRC_2, ALUOP_2, control_2[1:0]}));
  or or_3 (or_3_out, J_flush, B_flush);
  RAM #(.addrWidth(20), .dataWidth(32), .bus("separate")) ram_2 (
    .addr(out_6[19:0]), .din(bus_b_2), .data(ram_2_data), .sel(control_2[22]), .ld(clock_1_out),
    .clr(control_2[21]));  // open: str, clk
  MEM_WB mem_wb_1 (
    .Control({control_2[25:21], BNEZ_2, BLEZ_2, BGTZ_2, BGEZ_2, BLTZ_2, control_2[15:14], BEZ_2, BNE_2, BRANCH_2, control_2[10:8], ALUSRC_2, ALUOP_2, control_2[1:0]}),
    .ALU_out(out_6), .mem_out(ram_2_data), .Rd(RD2), .reg_dst(control_2[23]), .ALU_out_2(out_5),
    .mem_out_2(mem_wb_1_mem_out_2), .Rd_2(RD3), .reg_dst_2(out_4[23]), .clk(clock_1_out), .control_2(out_4));  // open: En
  Multiplexer #(.width(32), .enable("false")) multiplexer_11 (
    .in0(out_5), .in1(mem_wb_1_mem_out_2), .out(result), .sel(out_4[23]));

  assign out_8 = out_5;
  assign out_10 = out_7;
  assign out_12 = out_11;
  // also tied to GND on the sheet: adder_1_cout

  // Other names for the same wires on the sheet: _11imm[7:0] = _8imm; funct[1:0] = _8imm[1:0]; imm5[4:0] = _8imm[4:0];
  //   RT[2:0] = _8imm[4:2]; RS[2:0] = _8imm[7:5]; RD[2:0] = _11imm; alu_input[3:0] = out_7; control[25:0] = out_11;
  //   REG_DST = out_11[0]; RegWrite = out_11[1]; ALUOP[3:0] = out_11[5:2]; ALUSRC[1:0] = out_11[7:6]; J = out_11[8];
  //   JUMP = out_11[8]; JSELECT = out_11[9]; LINK = out_11[10]; BRANCH = out_11[11]; BNE = out_11[12];
  //   BEZ = out_11[13]; SHIFT[1:0] = out_11[15:14]; BLTZ = out_11[16]; BGEZ = out_11[17]; BGTZ = out_11[18];
  //   BLEZ = out_11[19]; BNEZ = out_11[20]; MOMREAD = out_11[21]; MOMWRITE = out_11[22]; MOMREG = out_11[23];
  //   SELECT = out_11[24]; dst2 = out_11[25]; control_1[25:0] = out_13; REG_DST_1 = out_13[0]; RegWrite_1 = out_13[1];
  //   ALUOP_1[3:0] = out_13[5:2]; ALUSRC_1[1:0] = out_13[7:6]; JUMP1 = out_13[8]; JSELECT_1 = out_13[9];
  //   LINK_1 = out_13[10]; BRANCH_1 = out_13[11]; BNE_1 = out_13[12]; BEZ_1 = out_13[13];
  //   SHIFT_1[1:0] = out_13[15:14]; BLTZ_1 = out_13[16]; BGEZ_1 = out_13[17]; BGTZ_1 = out_13[18];
  //   BLEZ_1 = out_13[19]; BNEZ_1 = out_13[20]; MOMREAD_1 = out_13[21]; MOMWRITE_1 = out_13[22];
  //   MOMREG_1 = out_13[23]; SELECT_1 = out_13[24]; dst2_1 = out_13[25]; REG_DST_2 = control_2[0];
  //   RegWrite_2 = control_2[1];
  //   control_2 (some bits) = {BNEZ_2, BLEZ_2, BGTZ_2, BGEZ_2, BLTZ_2, BEZ_2, BNE_2, BRANCH_2, ALUSRC_2, ALUOP_2};
  //   JUMP_2 = control_2[8]; JSELECT_2 = control_2[9]; LINK_2 = control_2[10]; SHIFT_2[1:0] = control_2[15:14];
  //   MOMREAD_2 = control_2[21]; MOMWRITE_2 = control_2[22]; MOMREG_2 = control_2[23]; SELECT_2 = control_2[24];
  //   dst2_2 = control_2[25]; control_3[25:0] = out_4; REG_DST_3 = out_4[0]; RegWrite_3 = out_4[1];
  //   ALUOP_3[3:0] = out_4[5:2]; ALUSRC_3[1:0] = out_4[7:6]; JUMP_3 = out_4[8]; JSELECT_3 = out_4[9];
  //   LINK_3 = out_4[10]; BRANCH_3 = out_4[11]; BNE_3 = out_4[12]; BEZ_3 = out_4[13]; SHIFT_3[1:0] = out_4[15:14];
  //   BLTZ_3 = out_4[16]; BGEZ_3 = out_4[17]; BGTZ_3 = out_4[18]; BLEZ_3 = out_4[19]; BNEZ_3 = out_4[20];
  //   MOMREAD_3 = out_4[21]; MOMWRITE_3 = out_4[22]; MOMREG_3 = out_4[23]; SELECT_3 = out_4[24]; dst2_3 = out_4[25];
  //   Eorward_B[1:0] = out_9; Forward_A[1:0] = out_3

  // Notes on the sheet:
  //   CONTROL UNIT
  //   pc next
  //   control alu
endmodule

module Register_File (
  input  [2:0] Rt,
  input  [2:0] Rs,
  input  [2:0] RD,
  input  [31:0] BUS_W,
  input  RegWrite,
  input  in_6,
  output [31:0] BUS_B,
  output [31:0] BUS_A
);

  wire and_1_out, and_2_out, and_3_out, and_4_out, and_5_out, and_6_out, and_7_out, and_8_out,
       decoder_1_out0, decoder_1_out1, decoder_1_out2, decoder_1_out3, decoder_1_out4, decoder_1_out5,
       decoder_1_out6, decoder_1_out7;
  wire [31:0] register_1_q, register_2_q, register_3_q, register_4_q, register_5_q, register_6_q,
       register_7_q, register_8_q;

  Decoder #(.select(3), .enable("false")) decoder_1 (
    .out0(decoder_1_out0), .out1(decoder_1_out1), .out2(decoder_1_out2), .out3(decoder_1_out3),
    .out4(decoder_1_out4), .out5(decoder_1_out5), .out6(decoder_1_out6), .out7(decoder_1_out7), .sel(RD));
  and and_1 (and_1_out, decoder_1_out0, RegWrite);
  and and_2 (and_2_out, decoder_1_out1, RegWrite);
  and and_3 (and_3_out, decoder_1_out2, RegWrite);
  and and_4 (and_4_out, decoder_1_out3, RegWrite);
  and and_5 (and_5_out, decoder_1_out4, RegWrite);
  and and_6 (and_6_out, decoder_1_out5, RegWrite);
  and and_7 (and_7_out, decoder_1_out6, RegWrite);
  and and_8 (and_8_out, decoder_1_out7, RegWrite);
  Register #(.width(32)) register_1 (.D(BUS_W), .en(and_1_out), .Q(register_1_q), .clk(in_6));  // open: clr
  Register #(.width(32)) register_2 (.D(BUS_W), .en(and_2_out), .Q(register_2_q), .clk(in_6));  // open: clr
  Register #(.width(32)) register_3 (.D(BUS_W), .en(and_3_out), .Q(register_3_q), .clk(in_6));  // open: clr
  Register #(.width(32)) register_4 (.D(BUS_W), .en(and_4_out), .Q(register_4_q), .clk(in_6));  // open: clr
  Register #(.width(32)) register_5 (.D(BUS_W), .en(and_5_out), .Q(register_5_q), .clk(in_6));  // open: clr
  Register #(.width(32)) register_6 (.D(BUS_W), .en(and_6_out), .Q(register_6_q), .clk(in_6));  // open: clr
  Register #(.width(32)) register_7 (.D(BUS_W), .en(and_7_out), .Q(register_7_q), .clk(in_6));  // open: clr
  Register #(.width(32)) register_8 (.D(BUS_W), .en(and_8_out), .Q(register_8_q), .clk(in_6));  // open: clr
  Multiplexer #(.select(3), .width(32), .enable("false")) multiplexer_1 (
    .in0(register_1_q), .in1(register_2_q), .in2(register_3_q), .in3(register_4_q), .in4(register_5_q),
    .in5(register_6_q), .in6(register_7_q), .in7(register_8_q), .out(BUS_B), .sel(Rt));
  Multiplexer #(.select(3), .width(32), .enable("false")) multiplexer_2 (
    .in0(register_1_q), .in1(register_2_q), .in2(register_3_q), .in3(register_4_q), .in4(register_5_q),
    .in5(register_6_q), .in6(register_7_q), .in7(register_8_q), .out(BUS_A), .sel(Rs));
endmodule

module ALU (
  input  [31:0] RS,
  input  [31:0] RT,
  input  [3:0] alu_in,
  input  [1:0] shift,
  output [31:0] output_alu,
  output zero,
  output zerogtz,
  output zeroeqz,
  output zeroltz,
  output zerogez,
  output zerolez
);

  wire adder_1_cout, adder_2_cout, comparator_1_lt, comparator_3_eq, comparator_3_gt, comparator_3_lt;
  wire [4:0] bit_extender_1_out;
  wire [31:0] adder_1_out, adder_2_out, and_1_out, bit_extender_2_out, bit_extender_3_out, multiplexer_1_out,
       or_1_out, shifter_1_out, shifter_2_out, shifter_3_out, subtractor_1_out, xor_1_out, xor_2_out;

  Bit_Extender #(.in_width(32), .out_width(5), .\type ("sign")) bit_extender_1 (.in(RT), .out(bit_extender_1_out));
  Adder #(.width(32)) adder_1 (.a(RS), .b(32'h1), .out(adder_1_out), .cout(adder_1_cout));  // open: cin
  assign and_1_out = RS & RT;  // AND_Gate and_1, 32 bits wide
  assign or_1_out = RS | RT;  // OR_Gate or_1, 32 bits wide
  assign xor_1_out = RS ^ RT;  // XOR_Gate xor_1, 32 bits wide
  assign xor_2_out = adder_1_out ^ RT;  // XOR_Gate xor_2, 32 bits wide
  Adder #(.width(32)) adder_2 (.a(RS), .b(RT), .out(adder_2_out), .cin(1'b0), .cout(adder_2_cout));
  Subtractor #(.width(32)) subtractor_1 (.a(RS), .b(RT), .out(subtractor_1_out));  // open: bin, bout
  Comparator #(.width(32)) comparator_1 (.a(RS), .b(RT), .eq(zero), .lt(comparator_1_lt));  // open: gt
  Shifter #(.width(32)) shifter_1 (.in(RS), .\dist (bit_extender_1_out), .out(shifter_1_out));
  Shifter #(.width(32), .shift("lr")) shifter_2 (.in(RS), .\dist (bit_extender_1_out), .out(shifter_2_out));
  Shifter #(.width(32), .shift("rr")) shifter_3 (.in(RS), .\dist (bit_extender_1_out), .out(shifter_3_out));
  Comparator #(.width(32)) comparator_2 (.a(RT), .b({32{1'b0}}), .gt(zerogtz), .eq(zeroeqz), .lt(zeroltz));
  Comparator #(.width(32)) comparator_3 (
    .a(RT), .b({32{1'b0}}), .gt(comparator_3_gt), .eq(comparator_3_eq), .lt(comparator_3_lt));
  assign bit_extender_2_out = {{31{zero}}, zero};  // Bit_Extender bit_extender_2
  assign bit_extender_3_out = {{31{1'b0}}, comparator_1_lt};  // Bit_Extender bit_extender_3
  and and_2 (zerogez, comparator_3_gt, comparator_3_eq);
  and and_3 (zerolez, comparator_3_eq, comparator_3_lt);
  Multiplexer #(.select(2), .width(32), .enable("false")) multiplexer_1 (
    .in0(shifter_1_out), .in1(shifter_2_out), .in3(shifter_3_out), .out(multiplexer_1_out), .sel(shift));  // open: in2
  Multiplexer #(.select(4), .width(32), .enable("false")) multiplexer_2 (
    .in0(and_1_out), .in1(or_1_out), .in2(xor_1_out), .in3(xor_2_out), .in4(adder_2_out),
    .in5(subtractor_1_out), .in6(bit_extender_3_out), .in7(bit_extender_2_out), .in8(multiplexer_1_out),
    .in9(RT), .in10({RS[23:0], RT[7:0]}), .in11({32{1'b0}}), .in12({32{1'b0}}), .in13({32{1'b0}}),
    .in14({32{1'b0}}), .in15({32{1'b0}}), .out(output_alu), .sel(alu_in));
  // also tied to GND on the sheet: adder_1_cout
endmodule

module control_unit (
  input  [4:0] in_1,
  output REG_DST,
  output REGWRITE,
  output [3:0] ALUOP,
  output [1:0] ALUSRC,
  output JUMP,
  output JSELECT,
  output LINK,
  output BRANCH,
  output BNE,
  output BEZ,
  output BLTZ,
  output BGEZ,
  output BGTZ,
  output BLEZ,
  output BNEZ,
  output MOMREAD,
  output MOMWRITE,
  output MOMREG,
  output SELECT,
  output dst2,
  output [1:0] SHIFT
);

  wire and_15_out, and_16_out, not_1_out, not_2_out, not_3_out, not_4_out, not_5_out, not_6_out, not_7_out,
       not_8_out, not_9_out, not_10_out, not_11_out, not_12_out, not_13_out, not_14_out, not_15_out,
       not_16_out, not_17_out, not_18_out, not_19_out, not_20_out, not_21_out, not_22_out, not_23_out,
       not_24_out, not_25_out, not_26_out, not_27_out, not_28_out, not_29_out, not_30_out, not_31_out,
       not_32_out, not_33_out, not_34_out;

  not not_1 (not_1_out, in_1[2]);
  not not_2 (not_2_out, in_1[4]);
  not not_3 (not_3_out, in_1[0]);
  not not_4 (not_4_out, in_1[4]);
  not not_5 (not_5_out, in_1[3]);
  not not_6 (not_6_out, in_1[1]);
  not not_7 (not_7_out, in_1[0]);
  not not_8 (not_8_out, in_1[3]);
  not not_9 (not_9_out, in_1[0]);
  not not_10 (not_10_out, in_1[3]);
  not not_11 (not_11_out, in_1[2]);
  not not_12 (not_12_out, in_1[1]);
  not not_13 (not_13_out, in_1[0]);
  not not_14 (not_14_out, in_1[2]);
  not not_15 (not_15_out, in_1[1]);
  not not_16 (not_16_out, in_1[3]);
  not not_17 (not_17_out, in_1[1]);
  not not_18 (not_18_out, in_1[3]);
  not not_19 (not_19_out, in_1[2]);
  not not_20 (not_20_out, in_1[1]);
  not not_21 (not_21_out, in_1[0]);
  not not_22 (not_22_out, in_1[3]);
  not not_23 (not_23_out, in_1[2]);
  not not_24 (not_24_out, in_1[1]);
  not not_25 (not_25_out, in_1[3]);
  not not_26 (not_26_out, in_1[2]);
  not not_27 (not_27_out, in_1[1]);
  not not_28 (not_28_out, in_1[0]);
  not not_29 (not_29_out, in_1[3]);
  not not_30 (not_30_out, in_1[2]);
  not not_31 (not_31_out, in_1[1]);
  not not_32 (not_32_out, in_1[1]);
  not not_33 (not_33_out, in_1[4]);
  not not_34 (not_34_out, in_1[1]);
  regdet regdet_1 (.in_1(in_1), .out_2(REG_DST));
  regwrite regwrite_1 (.in_1(in_1), .REGWRITE(REGWRITE));
  ALUOP aluop_1 (.in_1(in_1), .out_2(ALUOP));
  ALUSRC alusrc_1 (.in_1(in_1), .out_2(ALUSRC));
  and and_1 (JUMP, in_1[4], in_1[3], in_1[1]);
  and and_2 (JSELECT, in_1[4], in_1[3], not_1_out, in_1[1]);
  and and_3 (LINK, in_1[4], in_1[3], in_1[1], in_1[0]);
  and and_4 (BRANCH, not_2_out, in_1[3], in_1[2], in_1[1], not_3_out);
  and and_5 (BNE, not_4_out, in_1[3], in_1[2], in_1[1], in_1[0]);
  and and_6 (BEZ, in_1[4], not_5_out, in_1[2], not_6_out, not_7_out);
  and and_7 (BLTZ, in_1[4], not_8_out, in_1[2], in_1[1], not_9_out);
  and and_8 (BGEZ, in_1[4], not_10_out, in_1[2], in_1[1], in_1[0]);
  and and_9 (BGTZ, in_1[4], in_1[3], not_11_out, not_12_out, not_13_out);
  and and_10 (BLEZ, in_1[4], in_1[3], not_14_out, not_15_out, in_1[0]);
  and and_11 (BNEZ, in_1[4], not_16_out, in_1[2], not_17_out, in_1[0]);
  and and_12 (MOMREAD, in_1[4], not_18_out, not_19_out, not_20_out, not_21_out);
  and and_13 (MOMWRITE, in_1[4], not_22_out, not_23_out, not_24_out, in_1[0]);
  and and_14 (MOMREG, in_1[4], not_25_out, not_26_out, not_27_out, not_28_out);
  and and_15 (and_15_out, in_1[4], not_29_out, in_1[2]);
  and and_16 (and_16_out, in_1[4], in_1[3], not_30_out, not_31_out);
  and and_17 (dst2, in_1[4], in_1[3], in_1[2], not_32_out, in_1[0]);
  and and_18 (SHIFT[0], not_33_out, in_1[3], in_1[2], not_34_out);
  and and_19 (SHIFT[1], SHIFT[0], in_1[0]);
  or or_1 (SELECT, and_15_out, and_16_out);

  // Notes on the sheet:
  //   A
  //   E
  //   D
  //   B
endmodule

module ALUOP (
  input  [4:0] in_1,
  output [3:0] out_2
);

  aluopout1 aluopout1_1 (.in_1(in_1), .out_2(out_2[0]));
  aluopout2 aluopout2_1 (.in_1(in_1), .out_2(out_2[1]));
  aluopout3 aluopout3_1 (.in_1(in_1), .out_2(out_2[2]));
  aluopout4 aluopout4_1 (.in_1(in_1), .out_2(out_2[3]));
endmodule

module regdet (
  input  [4:0] in_1,
  output out_2
);

  wire and_1_out, and_2_out, and_3_out, and_4_out, not_1_out, not_2_out, not_3_out, not_4_out, not_5_out,
       not_6_out;

  not not_1 (not_1_out, in_1[4]);
  not not_2 (not_2_out, in_1[3]);
  not not_3 (not_3_out, in_1[2]);
  not not_4 (not_4_out, in_1[3]);
  not not_5 (not_5_out, in_1[2]);
  not not_6 (not_6_out, in_1[1]);
  and and_1 (and_1_out, not_1_out, in_1[3], in_1[2], in_1[1]);
  and and_2 (and_2_out, in_1[4], not_2_out, in_1[2]);
  and and_3 (and_3_out, in_1[4], in_1[3], not_3_out);
  and and_4 (and_4_out, in_1[4], not_4_out, not_5_out, not_6_out, in_1[0]);
  or or_1 (out_2, and_1_out, and_2_out, and_3_out, and_4_out);
endmodule

module ALUSRC (
  input  [4:0] in_1,
  output [1:0] out_2
);

  wire and_1_out, and_2_out, and_3_out, and_4_out, not_1_out, not_2_out, not_3_out, not_4_out, not_5_out,
       not_6_out, not_7_out, not_8_out, not_9_out;

  not not_1 (not_1_out, in_1[4]);
  not not_2 (not_2_out, in_1[3]);
  not not_3 (not_3_out, in_1[2]);
  not not_4 (not_4_out, in_1[1]);
  not not_5 (not_5_out, in_1[4]);
  not not_6 (not_6_out, in_1[3]);
  not not_7 (not_7_out, in_1[2]);
  not not_8 (not_8_out, in_1[1]);
  not not_9 (not_9_out, in_1[1]);
  and and_1 (and_1_out, not_1_out, not_2_out, not_3_out, not_4_out);
  and and_2 (and_2_out, not_5_out, in_1[3], in_1[2], in_1[1]);
  and and_3 (and_3_out, in_1[4], not_6_out, in_1[2]);
  and and_4 (and_4_out, in_1[4], in_1[3], not_7_out, not_8_out);
  and and_5 (out_2[0], in_1[4], in_1[3], in_1[2], not_9_out);
  or or_1 (out_2[1], and_1_out, and_2_out, and_3_out, and_4_out);
endmodule

module regwrite (
  input  [4:0] in_1,
  output REGWRITE
);

  wire and_1_out, and_2_out, and_3_out, and_4_out, and_5_out, and_6_out, not_1_out, not_2_out, not_3_out,
       not_4_out, not_5_out, not_6_out, not_7_out, not_8_out, not_9_out, not_10_out, not_11_out, not_12_out;

  not not_1 (not_1_out, in_1[4]);
  not not_2 (not_2_out, in_1[3]);
  not not_3 (not_3_out, in_1[1]);
  not not_4 (not_4_out, in_1[4]);
  not not_5 (not_5_out, in_1[3]);
  not not_6 (not_6_out, in_1[4]);
  not not_7 (not_7_out, in_1[2]);
  not not_8 (not_8_out, in_1[1]);
  not not_9 (not_9_out, in_1[3]);
  not not_10 (not_10_out, in_1[2]);
  not not_11 (not_11_out, in_1[1]);
  not not_12 (not_12_out, in_1[0]);
  and and_1 (and_1_out, in_1[4], in_1[3], in_1[1], in_1[0]);
  and and_2 (and_2_out, not_1_out, not_2_out, not_3_out);
  and and_3 (and_3_out, not_4_out, not_5_out, in_1[2], in_1[1]);
  and and_4 (and_4_out, not_6_out, in_1[3], not_7_out);
  and and_5 (and_5_out, in_1[3], in_1[2], not_8_out);
  and and_6 (and_6_out, in_1[4], not_9_out, not_10_out, not_11_out, not_12_out);
  or or_1 (REGWRITE, and_2_out, and_3_out, and_4_out, and_5_out, and_6_out, and_1_out);
endmodule

module aluopout1 (
  input  [4:0] in_1,
  output out_2
);

  wire and_1_out, and_2_out, and_3_out, and_4_out, and_5_out, not_1_out, not_2_out, not_3_out, not_4_out,
       not_5_out, not_6_out, not_7_out, not_8_out, not_9_out, not_10_out, not_11_out;

  not not_1 (not_1_out, in_1[4]);
  not not_2 (not_2_out, in_1[3]);
  and and_1 (and_1_out, not_1_out, not_2_out, not_3_out, in_1[0]);
  not not_3 (not_3_out, in_1[1]);
  not not_4 (not_4_out, in_1[4]);
  and and_2 (and_2_out, not_4_out, in_1[3], not_5_out, in_1[0]);
  not not_5 (not_5_out, in_1[2]);
  not not_6 (not_6_out, in_1[4]);
  and and_3 (and_3_out, not_6_out, in_1[3], in_1[2], not_7_out);
  not not_7 (not_7_out, in_1[1]);
  not not_8 (not_8_out, in_1[4]);
  not not_9 (not_9_out, in_1[3]);
  and and_4 (and_4_out, not_8_out, not_9_out, in_1[2], in_1[1], in_1[0]);
  and and_5 (and_5_out, in_1[4], in_1[3], in_1[2], not_10_out, not_11_out);
  not not_10 (not_10_out, in_1[1]);
  not not_11 (not_11_out, in_1[0]);
  or or_1 (out_2, and_1_out, and_2_out, and_3_out, and_4_out, and_5_out);
endmodule

module aluopout2 (
  input  [4:0] in_1,
  output out_2
);

  wire and_1_out, and_2_out, and_3_out, and_4_out, not_1_out, not_2_out, not_3_out, not_4_out, not_5_out,
       not_6_out, not_7_out, not_8_out, not_9_out, not_10_out, not_11_out;

  not not_1 (not_1_out, in_1[4]);
  not not_2 (not_2_out, in_1[3]);
  not not_3 (not_3_out, in_1[1]);
  not not_4 (not_4_out, in_1[4]);
  not not_5 (not_5_out, in_1[2]);
  not not_6 (not_6_out, in_1[1]);
  not not_7 (not_7_out, in_1[3]);
  not not_8 (not_8_out, in_1[2]);
  not not_9 (not_9_out, in_1[1]);
  not not_10 (not_10_out, in_1[1]);
  not not_11 (not_11_out, in_1[0]);
  and and_1 (and_1_out, not_1_out, not_2_out, in_1[2], not_3_out);
  and and_2 (and_2_out, not_4_out, in_1[3], not_5_out, not_6_out);
  and and_3 (and_3_out, in_1[4], not_7_out, not_8_out, not_9_out);
  and and_4 (and_4_out, in_1[4], in_1[3], in_1[2], not_10_out, not_11_out);
  or or_1 (out_2, and_1_out, and_2_out, and_3_out, and_4_out);
endmodule

module aluopout3 (
  input  [4:0] in_1,
  output out_2
);

  wire and_1_out, and_2_out, and_3_out, not_1_out, not_2_out, not_3_out, not_4_out, not_5_out, not_6_out;

  not not_1 (not_1_out, in_1[4]);
  not not_2 (not_2_out, in_1[3]);
  not not_3 (not_3_out, in_1[4]);
  not not_4 (not_4_out, in_1[2]);
  not not_5 (not_5_out, in_1[1]);
  not not_6 (not_6_out, in_1[1]);
  and and_1 (and_1_out, not_1_out, not_2_out, in_1[2], in_1[1]);
  and and_2 (and_2_out, not_3_out, in_1[3], not_4_out, not_5_out);
  and and_3 (and_3_out, in_1[4], in_1[3], in_1[2], not_6_out, in_1[0]);
  or or_1 (out_2, and_1_out, and_2_out, and_3_out);
endmodule

module aluopout4 (
  input  [4:0] in_1,
  output out_2
);

  wire and_1_out, and_2_out, and_3_out, not_1_out, not_2_out, not_3_out, not_4_out, not_5_out, not_6_out;

  not not_1 (not_1_out, in_1[4]);
  not not_2 (not_2_out, in_1[2]);
  not not_3 (not_3_out, in_1[3]);
  not not_4 (not_4_out, in_1[2]);
  not not_5 (not_5_out, in_1[1]);
  not not_6 (not_6_out, in_1[1]);
  and and_1 (and_1_out, not_1_out, in_1[3], not_2_out, in_1[1]);
  and and_2 (and_2_out, in_1[4], not_3_out, not_4_out, not_5_out);
  and and_3 (and_3_out, in_1[3], in_1[2], not_6_out);
  or or_1 (out_2, and_1_out, and_2_out, and_3_out);
endmodule

// control alu
module ALUCONTROL (
  input  [3:0] aluop,
  input  [1:0] funct,
  output [3:0] out_3
);

  alucontrolbit1 alucontrolbit1_1 (.in_1(aluop), .in_2(funct), .out_3(out_3[0]));
  alucontrolbit2 alucontrolbit2_1 (.in_1(aluop), .in_2(funct), .out_3(out_3[1]));
  alucontrolbit3 alucontrolbit3_1 (.in_1(aluop), .out_2(out_3[2]));
  alucontrolbit4 alucontrolbit4_1 (.in_1(aluop), .out_2(out_3[3]));
endmodule

module alucontrolbit1 (
  input  [3:0] in_1,
  input  [1:0] in_2,
  output out_3
);

  wire and_1_out, and_2_out, and_3_out, and_4_out, not_1_out, not_2_out, not_3_out, not_4_out, not_5_out,
       not_6_out, not_7_out, not_8_out, not_9_out;

  not not_1 (not_1_out, in_1[3]);
  not not_2 (not_2_out, in_1[2]);
  not not_3 (not_3_out, in_1[1]);
  not not_4 (not_4_out, in_1[3]);
  not not_5 (not_5_out, in_1[1]);
  not not_6 (not_6_out, in_1[2]);
  not not_7 (not_7_out, in_1[1]);
  not not_8 (not_8_out, in_1[0]);
  not not_9 (not_9_out, in_1[2]);
  and and_1 (and_1_out, not_1_out, not_2_out, not_3_out, in_2[0]);
  and and_2 (and_2_out, not_4_out, in_1[2], not_5_out, in_1[0]);
  and and_3 (and_3_out, in_1[3], not_6_out, not_7_out, not_8_out);
  and and_4 (and_4_out, not_9_out, in_1[1], in_1[0]);
  or or_1 (out_3, and_1_out, and_2_out, and_3_out, and_4_out);

  // Notes on the sheet:
  //   E
  //   f
endmodule

module alucontrolbit2 (
  input  [3:0] in_1,
  input  [1:0] in_2,
  output out_3
);

  wire and_1_out, and_2_out, and_3_out, and_4_out, not_1_out, not_2_out, not_3_out, not_4_out, not_5_out,
       not_6_out, not_7_out, not_8_out;

  not not_1 (not_1_out, in_1[3]);
  not not_2 (not_2_out, in_1[2]);
  not not_3 (not_3_out, in_1[1]);
  not not_4 (not_4_out, in_1[3]);
  not not_5 (not_5_out, in_1[1]);
  not not_6 (not_6_out, in_1[3]);
  not not_7 (not_7_out, in_1[1]);
  not not_8 (not_8_out, in_1[0]);
  and and_1 (and_1_out, not_1_out, not_2_out, not_3_out, in_2[1]);
  and and_2 (and_2_out, not_4_out, in_1[2], not_5_out);
  and and_3 (and_3_out, not_6_out, in_1[2], in_1[1], in_1[0]);
  and and_4 (and_4_out, in_1[3], not_7_out, not_8_out);
  or or_1 (out_3, and_1_out, and_2_out, and_3_out, and_4_out);
endmodule

module alucontrolbit3 (
  input  [3:0] in_1,
  output out_2
);

  wire and_1_out, and_2_out, and_3_out, not_1_out, not_2_out, not_3_out, not_4_out, not_5_out, not_6_out;

  not not_1 (not_1_out, in_1[3]);
  not not_2 (not_2_out, in_1[2]);
  and and_1 (and_1_out, not_1_out, not_2_out, not_3_out, in_1[0]);
  not not_3 (not_3_out, in_1[1]);
  not not_4 (not_4_out, in_1[3]);
  and and_2 (and_2_out, not_4_out, in_1[2], in_1[1]);
  and and_3 (and_3_out, in_1[3], not_5_out, not_6_out);
  not not_5 (not_5_out, in_1[2]);
  not not_6 (not_6_out, in_1[0]);
  or or_1 (out_2, and_1_out, and_2_out, and_3_out);
endmodule

module alucontrolbit4 (
  input  [3:0] in_1,
  output out_2
);

  wire and_1_out, and_2_out, not_1_out, not_2_out, not_3_out;

  not not_1 (not_1_out, in_1[2]);
  not not_2 (not_2_out, in_1[1]);
  not not_3 (not_3_out, in_1[0]);
  and and_1 (and_1_out, in_1[3], not_1_out, in_1[0]);
  and and_2 (and_2_out, in_1[3], in_1[2], not_2_out, not_3_out);
  or or_1 (out_2, and_1_out, and_2_out);
endmodule

// jump
module JUMP (
  input  [10:0] _11_imm,
  input  [19:0] pc,
  input  JSELSCT,
  input  [31:0] reg_rd,
  input  [7:0] _8imm,
  output [19:0] jumpoutput
);

  wire adder_1_cout, adder_2_cout;
  wire [7:0] shifter_1_out;
  wire [10:0] shifter_2_out;
  wire [19:0] adder_1_out, bit_extender_2_out, bit_extender_3_out;
  wire [31:0] adder_2_out, bit_extender_1_out;

  Shifter shifter_1 (.in(_8imm), .\dist (3'b001), .out(shifter_1_out));
  Shifter #(.width(11)) shifter_2 (.in(_11_imm), .\dist (4'b0001), .out(shifter_2_out));
  assign bit_extender_1_out = {{24{shifter_1_out[7]}}, shifter_1_out};  // Bit_Extender bit_extender_1
  assign bit_extender_2_out = {{9{shifter_2_out[10]}}, shifter_2_out};  // Bit_Extender bit_extender_2
  Adder #(.width(20)) adder_1 (.a(bit_extender_2_out), .b(pc), .out(adder_1_out), .cout(adder_1_cout));  // open: cin
  Adder #(.width(32)) adder_2 (
    .a(reg_rd), .b(bit_extender_1_out), .out(adder_2_out), .cout(adder_2_cout));  // open: cin
  Bit_Extender #(.in_width(32), .out_width(20)) bit_extender_3 (.in(adder_2_out), .out(bit_extender_3_out));
  Multiplexer #(.width(20), .enable("false")) multiplexer_1 (
    .in0(adder_1_out), .in1(bit_extender_3_out), .out(jumpoutput), .sel(JSELSCT));
  // also tied to GND on the sheet: {adder_1_cout, adder_2_cout}

  // Notes on the sheet:
  //   J & JAL
  //   JR &JALR
endmodule

// branch
module btanch (
  input  BRANCH,
  input  zer0,
  input  BNE,
  input  BEQZ,
  input  zero_eqz,
  input  [19:0] PC,
  input  BNEZ,
  input  [4:0] _5IMM,
  input  BLTZ,
  input  zero_ltz,
  input  [7:0] _8IMM,
  input  BGEZ,
  input  SELECT,
  input  zero_gez,
  input  BGTZ,
  input  zero_gtz,
  input  BLEZ,
  input  zero_lez,
  output pcsrc,
  output [19:0] out_branch
);

  wire and_1_out, and_2_out, and_3_out, and_4_out, and_5_out, and_6_out, and_7_out, and_8_out, not_1_out,
       not_2_out;
  wire [19:0] multiplexer_1_out, shifter_1_out, shifter_2_out;
  wire [31:0] bit_extender_1_out, bit_extender_2_out;
  wire [31:20] shifter_1_out_2, shifter_2_out_2;

  not not_1 (not_1_out, zer0);
  not not_2 (not_2_out, zero_eqz);
  and and_1 (and_1_out, BRANCH, zer0);
  and and_2 (and_2_out, BNE, not_1_out);
  and and_3 (and_3_out, BEQZ, zero_eqz);
  and and_4 (and_4_out, BNEZ, not_2_out);
  and and_5 (and_5_out, BLTZ, zero_ltz);
  and and_6 (and_6_out, BGEZ, zero_gez);
  and and_7 (and_7_out, BGTZ, zero_gtz);
  and and_8 (and_8_out, BLEZ, zero_lez);
  or or_1 (pcsrc, and_1_out, and_2_out, and_3_out, and_4_out, and_5_out, and_6_out, and_7_out, and_8_out);
  assign bit_extender_1_out = {{27{_5IMM[4]}}, _5IMM};  // Bit_Extender bit_extender_1
  assign bit_extender_2_out = {{24{_8IMM[7]}}, _8IMM};  // Bit_Extender bit_extender_2
  Shifter #(.width(32)) shifter_1 (.in(bit_extender_1_out), .\dist (5'b00001), .out({shifter_1_out_2, shifter_1_out}));
  Shifter #(.width(32)) shifter_2 (.in(bit_extender_2_out), .\dist (5'b00001), .out({shifter_2_out_2, shifter_2_out}));
  Multiplexer #(.width(20), .enable("false")) multiplexer_1 (
    .in0(shifter_1_out), .in1(shifter_2_out), .out(multiplexer_1_out), .sel(SELECT));
  Adder #(.width(20)) adder_1 (.a(PC), .b(multiplexer_1_out), .out(out_branch));  // open: cin, cout

  // Notes on the sheet:
  //   select type branch
  //   branch operation
endmodule

module IF_ID (
  input  [19:0] Next_pc1,
  input  [15:0] ins,
  input  clock,
  input  clr,
  output [19:0] Next_pc_1,
  output [15:0] ins_2
);

  Register #(.width(20)) register_1 (.D(Next_pc1), .en(1'b1), .Q(Next_pc_1), .clk(clock), .clr(clr));
  Register #(.width(16)) register_2 (.D(ins), .en(1'b1), .Q(ins_2), .clk(clock), .clr(clr));
endmodule

module Hazerd_Unit (
  input  b,
  input  ID_EX_Jump,
  input  ID_EX_MemRead,
  input  [2:0] IF_ID_Rt,
  input  [2:0] ID_EX_Rd,
  input  [2:0] IF_ID_Rs,
  output b_flush,
  output JumpStall,
  output JumpFlush,
  output LoadStall
);

  wire comparator_1_eq, comparator_2_eq, or_1_out;

  buf buffer_1 (b_flush, b);
  buf buffer_2 (JumpFlush, ID_EX_Jump);
  Comparator #(.width(3)) comparator_1 (.a(IF_ID_Rt), .b(ID_EX_Rd), .eq(comparator_1_eq));  // open: gt, lt
  Comparator #(.width(3)) comparator_2 (.a(ID_EX_Rd), .b(IF_ID_Rs), .eq(comparator_2_eq));  // open: gt, lt
  and and_1 (LoadStall, ID_EX_MemRead, or_1_out);
  or or_1 (or_1_out, comparator_1_eq, comparator_2_eq);

  assign JumpStall = JumpFlush;
endmodule

module ID_EX (
  input  [19:0] Next_pc_2,
  input  [4:0] i_imm,
  input  [31:0] bus_a,
  input  [31:0] bus_b,
  input  [2:0] Rs,
  input  [2:0] Rt,
  input  [2:0] Rd,
  input  [10:0] J_imm_11,
  input  [7:0] B_imm,
  input  [25:0] control_1,
  input  [1:0] fu,
  input  CLK,
  input  clr,
  output [19:0] Next_pc2,
  output [4:0] i_imm1,
  output [31:0] bus_a_2,
  output [31:0] bus_b_2,
  output [2:0] Rs_Ex,
  output [2:0] Rt_Ex,
  output [2:0] Rd_Ex,
  output [10:0] J_imm1,
  output [7:0] B_imm1,
  output [25:0] control_2,
  output [1:0] fu2
);

  Register #(.width(20)) register_1 (.D(Next_pc_2), .en(1'b1), .Q(Next_pc2), .clk(CLK), .clr(clr));
  Register #(.width(5)) register_2 (.D(i_imm), .en(1'b1), .Q(i_imm1), .clk(CLK), .clr(clr));
  Register #(.width(32)) register_3 (.D(bus_a), .en(1'b1), .Q(bus_a_2), .clk(CLK), .clr(clr));
  Register #(.width(32)) register_4 (.D(bus_b), .en(1'b1), .Q(bus_b_2), .clk(CLK), .clr(clr));
  Register #(.width(3)) register_5 (.D(Rs), .en(1'b1), .Q(Rs_Ex), .clk(CLK), .clr(clr));
  Register #(.width(3)) register_6 (.D(Rt), .en(1'b1), .Q(Rt_Ex), .clk(CLK), .clr(clr));
  Register #(.width(3)) register_7 (.D(Rd), .en(1'b1), .Q(Rd_Ex), .clk(CLK), .clr(clr));
  Register #(.width(11)) register_8 (.D(J_imm_11), .en(1'b1), .Q(J_imm1), .clk(CLK), .clr(clr));
  Register register_9 (.D(B_imm), .en(1'b1), .Q(B_imm1), .clk(CLK), .clr(clr));
  Register #(.width(26)) register_10 (.D(control_1), .en(1'b1), .Q(control_2), .clk(CLK), .clr(clr));
  Register #(.width(2)) register_11 (.D(fu), .en(1'b1), .Q(fu2), .clk(CLK), .clr(clr));
endmodule

module EX_MEM (
  input  [25:0] Control,
  input  [19:0] PC,
  input  [31:0] BUS_A,
  input  [31:0] ALU_OUT,
  input  [31:0] BUS_B,
  input  [2:0] RS,
  input  [2:0] Rd,
  input  [2:0] RT,
  input  clk,
  input  clr,
  output [25:0] control_2,
  output [19:0] PC_2,
  output [31:0] BUS_A2,
  output [31:0] ALU_out_2,
  output [31:0] BUS_B2,
  output [2:0] RS_minus,
  output [2:0] Rd_minus,
  output [2:0] RT_minus
);

  Register #(.width(26)) register_1 (.D(Control), .en(1'b1), .Q(control_2), .clk(clk), .clr(clr));
  Register #(.width(20)) register_2 (.D(PC), .en(1'b1), .Q(PC_2), .clk(clk), .clr(clr));
  Register #(.width(32)) register_3 (.D(BUS_A), .en(1'b1), .Q(BUS_A2), .clk(clk), .clr(clr));
  Register #(.width(32)) register_4 (.D(ALU_OUT), .en(1'b1), .Q(ALU_out_2), .clk(clk), .clr(clr));
  Register #(.width(32)) register_5 (.D(BUS_B), .en(1'b1), .Q(BUS_B2), .clk(clk), .clr(clr));
  Register #(.width(3)) register_6 (.D(RS), .en(1'b1), .Q(RS_minus), .clk(clk), .clr(clr));
  Register #(.width(3)) register_7 (.D(Rd), .en(1'b1), .Q(Rd_minus), .clk(clk), .clr(clr));
  Register #(.width(3)) register_8 (.D(RT), .en(1'b1), .Q(RT_minus), .clk(clk), .clr(clr));
endmodule

module MEM_WB (
  input  [25:0] Control,
  input  [31:0] ALU_out,
  input  [31:0] mem_out,
  input  [2:0] Rd,
  input  reg_dst,
  input  clk,
  input  En,
  output [25:0] control_2,
  output [31:0] ALU_out_2,
  output [31:0] mem_out_2,
  output [2:0] Rd_2,
  output reg_dst_2
);

  Register #(.width(26)) register_1 (.D(Control), .Q(control_2), .clk(clk), .clr(En));  // open: en
  Register #(.width(32)) register_2 (.D(ALU_out), .Q(ALU_out_2), .clk(clk), .clr(En));  // open: en
  Register #(.width(32)) register_3 (.D(mem_out), .Q(mem_out_2), .clk(clk), .clr(En));  // open: en
  Register #(.width(3)) register_4 (.D(Rd), .Q(Rd_2), .clk(clk), .clr(En));  // open: en
  Register #(.width(1)) register_5 (.D(reg_dst), .Q(reg_dst_2), .clk(clk), .clr(En));  // open: en
endmodule

module Forward__Unit (
  input  [2:0] Mem_WB_Rd,
  input  [2:0] Rd_WB,
  input  RegWrt_Mem_WB,
  input  RegWrt_Ex_Mem,
  input  [2:0] Ra,
  input  [2:0] Rb,
  input  [2:0] Ex_Mem_Rd,
  input  RegWrt_WB,
  output [1:0] Forward_A,
  output [1:0] Forward_B
);

  wire and_1_out, and_2_out, and_3_out, and_4_out, and_5_out, and_6_out, comparator_1_eq, comparator_2_eq,
       comparator_3_eq, comparator_4_eq, comparator_5_eq, comparator_6_eq, or_1_out, or_2_out, or_3_out;

  Comparator #(.width(3)) comparator_1 (.a(Ex_Mem_Rd), .b(Ra), .eq(comparator_1_eq));  // open: gt, lt
  Comparator #(.width(3)) comparator_2 (.a(Ex_Mem_Rd), .b(Rb), .eq(comparator_2_eq));  // open: gt, lt
  Comparator #(.width(3)) comparator_3 (.a(Mem_WB_Rd), .b(Ra), .eq(comparator_3_eq));  // open: gt, lt
  Comparator #(.width(3)) comparator_4 (.a(Mem_WB_Rd), .b(Rb), .eq(comparator_4_eq));  // open: gt, lt
  or or_1 (or_1_out, Ex_Mem_Rd[0], Ex_Mem_Rd[1], Ex_Mem_Rd[2]);
  or or_2 (or_2_out, Mem_WB_Rd[0], Mem_WB_Rd[1], Mem_WB_Rd[2]);
  or or_3 (or_3_out, Rd_WB[0], Rd_WB[1], Rd_WB[2]);
  and and_1 (and_1_out, RegWrt_Ex_Mem, or_1_out, comparator_1_eq);
  and and_2 (and_2_out, RegWrt_Ex_Mem, or_1_out, comparator_2_eq);
  and and_3 (and_3_out, RegWrt_Mem_WB, comparator_3_eq, or_2_out);
  and and_4 (and_4_out, RegWrt_Mem_WB, comparator_4_eq, or_2_out);
  Comparator #(.width(3)) comparator_5 (.a(Rd_WB), .b(Ra), .eq(comparator_5_eq));  // open: gt, lt
  Comparator #(.width(3)) comparator_6 (.a(Rd_WB), .b(Rb), .eq(comparator_6_eq));  // open: gt, lt
  and and_5 (and_5_out, or_3_out, comparator_5_eq, RegWrt_WB);
  and and_6 (and_6_out, RegWrt_WB, comparator_6_eq, or_3_out);
  or or_4 (Forward_A[0], and_5_out, and_1_out);
  or or_5 (Forward_A[1], and_3_out, and_5_out);
  or or_6 (Forward_B[0], and_6_out, and_2_out);
  or or_7 (Forward_B[1], and_6_out, and_4_out);
endmodule
